# Fritzing sketch DCControlWithTransistor (saved by Fritzing 0.9.3b)
breadboards: 1

parts:
  Parça1 = Arduino Uno (Rev3)
  Q1 = NPN-Transistor [package="TO92 [THT]"]
  M1 = DC Motor
  D1 = Rectifier Diode [part_number=1N4001 package="300 mil [THT]"]
  R1 = Resistor [tolerance=±5% resistance=220 package=THT]
  R2 = Rotary Potentiometer (Small) [maximum_resistance=100kΩ package=THT]

nets:
  N1: Parça1.A0, R2.wiper
  N2: Parça1.GND, Q1.C, R2.leg2
  N3: Parça1.D3_PWM, R1.Pin_0
  N4: Parça1.5V, M1.pin_1, D1.cathode, R2.leg1
  N5: Q1.E, R1.Pin_1
  N6: M1.pin_2, D1.anode
