# Fritzing sketch PwmLedWithPot (saved by Fritzing 0.9.3b)
breadboards: 1

parts:
  Parça1 = Arduino Mega ADK (Rev3)
  R1 = Rotary Potentiometer (Large) [maximum_resistance=100kΩ package=THT]
  LED1 = smd LED [color="Red (633nm)" package="0603 [SMD]"]
  R2 = Resistor [tolerance=±5% resistance=220 package="0402 [SMD]"]

nets:
  N1: Parça1.A0, R1.wiper
  N2: Parça1.GND, R1.leg1, R1.leg2, R2.Pin_0
  N3: Parça1.D2_PWM, LED1.anode
  N4: LED1.cathode, R2.Pin_1
