# Fritzing sketch BrushedDCSpeedControlRPi (saved by Fritzing 0.9.3b)
breadboards: 1

parts:
  D1 = Rectifier Diode [part_number=1N4001 package="300 mil [THT]"]
  R1 = Resistor [tolerance=±5% resistance=220 package=THT]
  M1 = DC Motor
  Q1 = NPN-Transistor [package="TO92 [THT]"]
  Raspberry_Pi_1 = Raspberry Pi 3 [part_number=RPI-3-V1.2]
  IC1 = ULN2003A [package="DIP16 [THT]"]
  U1 = POT [package=pot_mammoth]

nets:
  N1: D1.cathode, M1.pin_2, Raspberry_Pi_1.5V, U1.S
  N2: D1.anode, M1.pin_1, Q1.E
  N3: R1.Pin_0, Q1.B
  N4: R1.Pin_1, Q1.C, Raspberry_Pi_1.GND, IC1.COM_-_Common, IC1.Out_3, U1.E
  N5: Raspberry_Pi_1.3v3, IC1.Out_2, IC1.Out_1
  N6: Raspberry_Pi_1.GIPO19, IC1.Out_5
  N7: Raspberry_Pi_1.GIPO20, IC1.Out_6
  N8: Raspberry_Pi_1.GIPO16, IC1.Out_4
  N9: Raspberry_Pi_1.GIPO25, IC1.Out_7
  N10: IC1.In_1, U1.A

notes:
  MCP3008
  Raspberry Pi 3 B+
