# Fritzing sketch ServoControlWithPot (saved by Fritzing 0.9.3b)
breadboards: 1

parts:
  Parça1 = Arduino Uno (Rev3)
  R1 = Rotary Potentiometer (Small) [maximum_resistance=100kΩ package=THT]
  J1 = Basic Servo

nets:
  N1: Parça1.A0, R1.wiper
  N2: Parça1.A1, J1.pulse
  5V: Parça1.5V, R1.leg2, J1.vcc
  GND: Parça1.GND, R1.leg1, J1.gnd
