# Fritzing sketch StepperControlWithPotOnArduino (saved by Fritzing 0.9.3b)
breadboards: 1

parts:
  Parça1 = Arduino Uno (Rev3)
  R1 = Rotary Potentiometer (Small) [maximum_resistance=100kΩ package=THT]
  M1 = Stepper Motor - Bipolar  # not connected

nets:
  N1: Parça1.A0, R1.wiper
  N2: Parça1.5V, R1.leg2
  N3: Parça1.GND, R1.leg1
